# Fritzing sketch VCO4069 (saved by Fritzing 0.9.6b)
breadboards: 1

parts:
  D2 = Diode [package=diode-1n4148]
  U2 = 74HC04_HEX_INVERTER [part_number=4069 package=dil14]
  C1 = Ceramic Capacitor [capacitance=2.2nF voltage=35V package="200 mil [THT, multilayer]"]
  R3 = Resistor [tolerance=±5% resistance=22k power=0.25 package=THT]
  R2 = Resistor [tolerance=±5% resistance=10k power=0.25 package=THT]
  R1 = Resistor [tolerance=±5% resistance=680 power=0.25 package=THT]
  C10 = Ceramic Capacitor [capacitance=0.22µF voltage=35V package="200 mil [THT, multilayer]"]
  D1 = Diode [package=diode-hv]
  R34 = Resistor [tolerance=±5% resistance=100k power=0.25 package=THT]
  R30 = Resistor [tolerance=±5% resistance=100k power=0.25 package=THT]
  R31 = Resistor [tolerance=±5% resistance=100k power=0.25 package=THT]
  R32 = Resistor [tolerance=±5% resistance=68k power=0.25 package=THT]
  R33 = Resistor [tolerance=±5% resistance=100k power=0.25 package=THT]
  R10 = Resistor [tolerance=±5% resistance=100k power=0.25 package=THT]
  R20 = Resistor [tolerance=±5% resistance=47k power=0.25 package=THT]
  R35 = Resistor [tolerance=±5% power=0.25 resistance=1M package=THT]
  R36 = Resistor [tolerance=±5% power=0.25 resistance=100k package=THT]
  R37 = Resistor [tolerance=±5% power=0.25 resistance=100k package=THT]
  R40 = Resistor [tolerance=±5% power=0.25 resistance=1M package=THT]
  NTC41 = Temperature Sensor (Thermistor) [thermistor_type=NTC package=THT]
  R43 = TRIMPOT [package=trim_pot_pth]
  R41 = Resistor [tolerance=±5% power=0.25 resistance=100k package=THT]
  R42 = Resistor [tolerance=±5% power=0.25 resistance=100k package=THT]
  R44 = Resistor [tolerance=±5% power=0.25 resistance=1.5k package=THT]
  Tune = POT [part_number=Tune package=alps_pot]
  NTC42 = Temperature Sensor (Thermistor) [thermistor_type=NTC package=THT]
  PW = POT [part_number=PW package=alps_pot]
  Pulse = mystery part, 1 pin [chip_label=Pulse]
  Saw = mystery part, 1 pin [chip_label=Saw]
  T2 = NPN-Transistor [package="TO92 [THT]"]
  T3 = NPN-Transistor [package="TO92 [THT]"]
  T1 = PNP-Transistor [package="TO92 [THT]"]
  NTC43 = Temperature Sensor (Thermistor) [thermistor_type=NTC package=THT]
  R43_2 = Resistor [tolerance=±5% power=0.25 resistance=100k package=THT]
  CV_in1 = mystery part, 1 pin [chip_label="CV in1"]
  CV_in2 = mystery part, 1 pin [chip_label="CV in2"]
  PWM = mystery part, 1 pin [chip_label=PWM]
  C30 = Ceramic Capacitor [capacitance=0.22µF voltage=35V package="200 mil [THT, multilayer]"]

nets:
  N1: D2.A, U2.3Y, R3.Pin_1
  N2: D2.C, U2.1A, C1.0, T2.C
  N3: U2.1Y, R2.Pin_0, R1.Pin_0, C10.1, D1.C, R20.Pin_0
  N4: U2.2A, R3.Pin_0, R2.Pin_1
  N5: U2.2Y, U2.3A
  GND: U2.GND, R10.Pin_0, R35.Pin_1, R37.Pin_1, R44.Pin_1, Tune.A, PW.E, T2.E
  N6: U2.4Y, C30.0
  N7: U2.4A, U2.5Y
  N8: U2.5A, U2.6Y, R30.Pin_0
  N9: U2.6A, R30.Pin_1, R31.Pin_1, R32.Pin_0, R33.Pin_0, R20.Pin_1
  12V: U2.VCC, R32.Pin_1, R40.Pin_0, PW.A, T3.C
  N10: C1.1, R1.Pin_1, D1.A
  N11: C10.0, R10.Pin_1, Saw.pin1
  -12V: R34.Pin_0, Tune.E, T1.C
  N12: R34.Pin_1, R33.Pin_1, T3.E
  N13: R31.Pin_0, PW.S
  N14: R35.Pin_0, R36.Pin_1, T3.B
  N15: R36.Pin_0, PWM.pin1
  N16: R37.Pin_0, Pulse.pin1, C30.1
  N17: R40.Pin_1, T2.B, T1.E
  N18: NTC41.pin_0, R41.Pin_1
  N19: NTC41.pin_1, R43.CW, NTC42.pin_1, T1.B, NTC43.pin_1
  N20: R43.CCW, R44.Pin_0
  N21: R41.Pin_0, Tune.S
  N22: R42.Pin_0, NTC42.pin_0
  N23: R42.Pin_1, CV_in1.pin1
  N24: NTC43.pin_0, R43_2.Pin_0
  N25: R43_2.Pin_1, CV_in2.pin1
