# Fritzing sketch VG1 (saved by Fritzing 0.9.6b)
breadboards: 1

parts:
  C4 = Electrolytic Capacitor [capacitance=22µF voltage=50V package="100 mil [THT, electrolytic]"]
  C5 = Electrolytic Capacitor [capacitance=22µF voltage=50V package="100 mil [THT, electrolytic]"]
  R1 = Resistor [tolerance=±5% power=0.25 resistance=5.36k package=THT]
  R2 = Resistor [tolerance=±5% power=0.25 resistance=5.36k package=THT]
  U3 = Zener Diode [part_number=LM336Z2.5 breakdown_voltage=3.6V package="300 mil [THT]"]
  D1 = Rectifier Diode [part_number=1N4002 package="300 mil [THT]"]
  R3 = Resistor [tolerance=±5% power=0.25 resistance=1 package=THT]
  R4 = Resistor [tolerance=±5% power=0.25 resistance=1 package=THT]
  D3 = Rectifier Diode [part_number=1N4002 package="300 mil [THT]"]
  D4 = Rectifier Diode [part_number=1N4002 package="300 mil [THT]"]
  V3 = DC Power [voltage=9V]
  C2 = Electrolytic Capacitor [capacitance=1mF voltage=25V package="200 mil [THT, electrolytic]"]
  C3 = Electrolytic Capacitor [capacitance=1mF voltage=25V package="200 mil [THT, electrolytic]"]
  C1 = Electrolytic Capacitor [capacitance=470µF voltage=50V package="200 mil [THT, electrolytic]"]
  + = mystery part, 1 pin [chip_label=+Vout]
  - = mystery part, 1 pin [chip_label=-Vout]
  GND = mystery part, 1 pin [chip_label=GND]
  D5 = Rectifier Diode [part_number=1N4002 package="300 mil [THT]"]
  U1 = Voltage Regulator [package=to220-adj]
  U2 = Voltage Regulator [package=to220-adj]
  +_2 = mystery part, 1 pin [chip_label=+Vin]
  -_2 = mystery part, 1 pin [chip_label=-Vin]

nets:
  N1: C4.-, R1.Pin_0, U3.cathode, D5.cathode, U2.ADJ
  N2: C4.+, R1.Pin_1, D3.cathode, V3.V+, C2.+, C1.+, +.pin1, U1.IN, +_2.pin1
  N3: C5.-, R2.Pin_0, D4.anode, V3.V-, C3.-, C1.-, -.pin1, U2.IN, -_2.pin1
  N4: C5.+, R2.Pin_1, U3.anode, D1.anode, U1.ADJ
  N5: D1.cathode, R3.Pin_1, U1.OUT
  GND: R3.Pin_0, R4.Pin_1, D3.anode, D4.cathode, C2.-, C3.+, GND.pin1
  N6: R4.Pin_0, D5.anode, U2.OUT

notes:
  R1 or R2 = (Vrr - 2.5) / .002 / 2

custom parts:
  Voltage Regulator: Voltage Regulator Standard LM317T adjustable voltage regulator. AOI (Adjust Output Input).
  Voltage Regulator: Voltage Regulator Standard LM337T adjustable negative voltage regulator. AIO (Adjust Input Output).
